// Logisim project Assignment8.circ as structural Verilog: 1 circuit, main circuit Control
module Control (
  input  [3:0] Opcode,
  input  [2:0] Funct,
  output MemtoReg,
  output Branch,
  output MemWrite,
  output RegWrite,
  output ALUSrc,
  output RegDst,
  output [2:0] ALUOp
);

  wire addi_out, and_1_out;
  wire [2:0] multiplexer_1_out;

  and and_1 (and_1_out, ~Opcode[3], ~Opcode[2], Opcode[1], Opcode[0]);  // AND_Gate
  Multiplexer #(.enable("false"), .width(3)) multiplexer_1 (
    .in0(3'b010), .in1(3'b110), .out(multiplexer_1_out), .sel(and_1_out));
  and lw (MemtoReg, Opcode[0], ~Opcode[1], ~Opcode[2], ~Opcode[3]);  // AND_Gate
  and beq (Branch, Opcode[0], Opcode[1], ~Opcode[2], ~Opcode[3]);  // AND_Gate
  and sw (MemWrite, ~Opcode[0], Opcode[1], ~Opcode[2], ~Opcode[3]);  // AND_Gate
  and addi (addi_out, Opcode[0], ~Opcode[1], Opcode[2], ~Opcode[3]);  // AND_Gate
  and r_format (RegDst, ~Opcode[0], ~Opcode[1], ~Opcode[2], ~Opcode[3]);  // AND_Gate
  Multiplexer #(.enable("false"), .width(3)) multiplexer_2 (
    .in0(multiplexer_1_out), .in1(Funct), .out(ALUOp), .sel(RegDst));
  or or_1 (RegWrite, MemtoReg, addi_out, RegDst);
  or or_2 (ALUSrc, MemtoReg, MemWrite, addi_out);
endmodule
